# Fritzing sketch pico2w-dht22-ssd1306 (saved by Fritzing 1.0.7)
breadboards: 1

parts:
  Pico/Pico2_Mod_1 = Raspberry Pi Pico or Pico 2
  DHT1 = DHT22 Humidity and Temperature Sensor
  Part1 = OLED Monochrome 128x64 0.96 inch [part_number=326]
  R1 = Resistor [tolerance=±1% power=0.25W resistance=10k package=THT]

nets:
  GND: Pico/Pico2_Mod_1.pin_3, Pico/Pico2_Mod_1.pin_8, Pico/Pico2_Mod_1.pin_13, Pico/Pico2_Mod_1.pin_18, Pico/Pico2_Mod_1.pin_23, Pico/Pico2_Mod_1.pin_28, Pico/Pico2_Mod_1.pin_33, Pico/Pico2_Mod_1.pin_38, DHT1.GND, Part1.GND
  N1: Pico/Pico2_Mod_1.pin_20, DHT1.DATA, R1.Pin_1
  N2: Pico/Pico2_Mod_1.pin_21, Part1.MOSI_SDA
  N3: Pico/Pico2_Mod_1.pin_22, Part1.SCLK_SCK
  VDD: Pico/Pico2_Mod_1.pin_36, DHT1.VDD, Part1.3.3V, R1.Pin_0

custom parts:
  Raspberry Pi Pico or Pico 2: Raspberry Pi Pico and Pico 2. Based around the RP2040 and RP2350 microcontrollers respectively, Picos are low cost microcontroller device bringing Raspberry Pi quality, cost, and easy of use to the microcontroller space. Jan 2021, Split part in to two versions: tht (this one) and SMD. This one will drill holes for a .1 in header in pcb to allow plugging in the module as well as providing pads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
